// Logisim project ALU.circ as structural Verilog: 2 circuits, main circuit Test
module Test (
  input  [1:0] in_1,
  input  [4:0] A,
  input  [4:0] B,
  output out_4,
  output out_5,
  output out_6
);

  wire bcd_to_7_seg_1_a, bcd_to_7_seg_1_b, bcd_to_7_seg_1_c, bcd_to_7_seg_1_d, bcd_to_7_seg_1_e,
       bcd_to_7_seg_1_f, bcd_to_7_seg_1_g, bcd_to_7_seg_2_a, bcd_to_7_seg_2_b, bcd_to_7_seg_2_c,
       bcd_to_7_seg_2_d, bcd_to_7_seg_2_e, bcd_to_7_seg_2_f, bcd_to_7_seg_2_g, bcd_to_7_seg_3_a,
       bcd_to_7_seg_3_b, bcd_to_7_seg_3_c, bcd_to_7_seg_3_d, bcd_to_7_seg_3_e, bcd_to_7_seg_3_f,
       bcd_to_7_seg_3_g;
  wire [3:0] binary_to_bcd_1_out_2, binary_to_bcd_1_out_3, binary_to_bcd_1_out_4;
  wire [7:0] alu_1_out_7;

  ALU alu_1 (.ZERO_FLAG(out_5), .SIGN_FLAG(out_4), .out_6(out_6), .in_3(in_1), .in_2(B), .in_1(A), .out_7(alu_1_out_7));
  Binary_to_BCD binary_to_bcd_1 (
    .in_1(alu_1_out_7), .out_4(binary_to_bcd_1_out_4), .out_3(binary_to_bcd_1_out_3),
    .out_2(binary_to_bcd_1_out_2));
  BCD_to_7_SEG bcd_to_7_seg_1 (
    .in_1(binary_to_bcd_1_out_4), .a(bcd_to_7_seg_1_a), .b(bcd_to_7_seg_1_b), .c(bcd_to_7_seg_1_c),
    .d(bcd_to_7_seg_1_d), .e(bcd_to_7_seg_1_e), .f(bcd_to_7_seg_1_f), .g(bcd_to_7_seg_1_g));
  BCD_to_7_SEG bcd_to_7_seg_2 (
    .in_1(binary_to_bcd_1_out_3), .a(bcd_to_7_seg_2_a), .b(bcd_to_7_seg_2_b), .c(bcd_to_7_seg_2_c),
    .d(bcd_to_7_seg_2_d), .e(bcd_to_7_seg_2_e), .f(bcd_to_7_seg_2_f), .g(bcd_to_7_seg_2_g));
  BCD_to_7_SEG bcd_to_7_seg_3 (
    .in_1(binary_to_bcd_1_out_2), .a(bcd_to_7_seg_3_a), .b(bcd_to_7_seg_3_b), .c(bcd_to_7_seg_3_c),
    .d(bcd_to_7_seg_3_d), .e(bcd_to_7_seg_3_e), .f(bcd_to_7_seg_3_f), .g(bcd_to_7_seg_3_g));
  _7_Segment_Display u_7_segment_display_1 (
    .g(bcd_to_7_seg_1_g), .f(bcd_to_7_seg_1_f), .a(bcd_to_7_seg_1_a), .b(bcd_to_7_seg_1_b),
    .e(bcd_to_7_seg_1_e), .d(bcd_to_7_seg_1_d), .c(bcd_to_7_seg_1_c));  // open: dp
  _7_Segment_Display u_7_segment_display_2 (
    .g(bcd_to_7_seg_2_g), .f(bcd_to_7_seg_2_f), .a(bcd_to_7_seg_2_a), .b(bcd_to_7_seg_2_b),
    .e(bcd_to_7_seg_2_e), .d(bcd_to_7_seg_2_d), .c(bcd_to_7_seg_2_c));  // open: dp
  _7_Segment_Display u_7_segment_display_3 (
    .g(bcd_to_7_seg_3_g), .f(bcd_to_7_seg_3_f), .a(bcd_to_7_seg_3_a), .b(bcd_to_7_seg_3_b),
    .e(bcd_to_7_seg_3_e), .d(bcd_to_7_seg_3_d), .c(bcd_to_7_seg_3_c));  // open: dp

  // Notes on the sheet:
  //   SIGN FLAG
  //   MODES OF OPERATION
  //   ZERO FLAG
  //   DIVISION BY ZERO
  //   UNITS
  //   TENS
  //   HUNDREDS
endmodule

module ALU (
  input  [4:0] in_1,
  input  [4:0] in_2,
  input  [1:0] in_3,
  output ZERO_FLAG,
  output SIGN_FLAG,
  output out_6,
  output [7:0] out_7
);

  wire and_1_out, and_2_out, and_3_out, and_4_out, n4_bit_comparator_1_e, n4_bit_comparator_2_e, not_1_out,
       not_2_out, or_1_out, or_2_out, or_3_out, or_4_out, or_5_out, or_6_out, or_9_out, or_11_out, or_14_out,
       or_16_out;
  wire [4:0] divider_1_out_6, substractor_1_p2;
  wire [5:0] addition_1_out_4;
  wire [8:0] n4by4_bit_multiplier_1_out_4;

  not not_1 (not_1_out, in_3[1]);
  not not_2 (not_2_out, in_3[0]);
  and and_1 (and_1_out, in_3[0], in_3[1]);
  and and_2 (and_2_out, not_1_out, in_3[0]);
  and and_3 (and_3_out, not_1_out, not_2_out);
  and and_4 (and_4_out, not_2_out, in_3[1]);
  // Substractor substractor_1: pin names not known; wires that end beside it: in_1, substractor_1_p2, in_2, and_2_out
  Addition addition_1 (.A(in_1), .out_4(addition_1_out_4), .B(in_2), .in_3(and_3_out));
  _4by4_Bit_Multiplier u_4by4_bit_multiplier_1 (
    .in_2(in_1), .in_1(in_2),
    .out_4({n4by4_bit_multiplier_1_out_4[8], out_7[7:5], n4by4_bit_multiplier_1_out_4[4:0]}), .in_3(and_4_out));
  Divider divider_1 (
    .DIVISOR(in_2), .out_6(divider_1_out_6), .DIVIDEND(in_1), .in_3(and_1_out), .out_7(out_6));  // open: out_5, SIGN_FLAG
  _4_bit_Comparator u_4_bit_comparator_1 (.in_1(4'b0000), .in_2(out_7[3:0]), .E(n4_bit_comparator_1_e));  // open: L
  or or_1 (or_1_out, divider_1_out_6[0], substractor_1_p2[0]);
  or or_2 (or_2_out, addition_1_out_4[0], n4by4_bit_multiplier_1_out_4[0]);
  or or_3 (or_3_out, divider_1_out_6[1], substractor_1_p2[1]);
  or or_4 (or_4_out, addition_1_out_4[1], n4by4_bit_multiplier_1_out_4[1]);
  or or_5 (or_5_out, divider_1_out_6[3], substractor_1_p2[3]);
  or or_6 (or_6_out, addition_1_out_4[3], n4by4_bit_multiplier_1_out_4[3]);
  and and_5 (ZERO_FLAG, n4_bit_comparator_1_e, n4_bit_comparator_2_e);
  _4_bit_Comparator u_4_bit_comparator_2 (.in_1(4'b0000), .in_2(out_7[7:4]), .E(n4_bit_comparator_2_e));  // open: L
  or or_7 (out_7[0], or_1_out, or_2_out);
  or or_8 (out_7[1], or_3_out, or_4_out);
  or or_9 (or_9_out, divider_1_out_6[2], substractor_1_p2[2]);
  or or_10 (out_7[2], or_9_out, or_11_out);
  or or_11 (or_11_out, addition_1_out_4[2], n4by4_bit_multiplier_1_out_4[2]);
  or or_12 (out_7[3], or_5_out, or_6_out);
  or or_13 (out_7[4], addition_1_out_4[4], n4by4_bit_multiplier_1_out_4[4]);
  or or_14 (or_14_out, divider_1_out_6[4], substractor_1_p2[4]);
  or or_15 (SIGN_FLAG, or_14_out, or_16_out);
  or or_16 (or_16_out, addition_1_out_4[5], n4by4_bit_multiplier_1_out_4[8]);

  // Notes on the sheet:
  //   DIVISION BY ZERO FLAG
endmodule
