// Logisim project Division.circ as structural Verilog: 8 circuits, main circuit main
module main (
  input  [4:0] in_1,
  input  [4:0] in_2,
  output ZERO_FLAG,
  output SIGN_FLAG,
  output out_5
);

  wire bcd_to_7_seg_1_a, bcd_to_7_seg_1_b, bcd_to_7_seg_1_c, bcd_to_7_seg_1_d, bcd_to_7_seg_1_e,
       bcd_to_7_seg_1_f, bcd_to_7_seg_1_g;
  wire [4:0] divider_1_out_6;

  Divider divider_1 (
    .DIVISOR(in_2), .out_5(ZERO_FLAG), .out_6(divider_1_out_6), .DIVIDEND(in_1), .SIGN_FLAG(SIGN_FLAG),
    .in_3(1'b1), .out_7(out_5));
  BCD_to_7_SEG bcd_to_7_seg_1 (
    .in_1(divider_1_out_6[3:0]), .a(bcd_to_7_seg_1_a), .b(bcd_to_7_seg_1_b), .c(bcd_to_7_seg_1_c),
    .d(bcd_to_7_seg_1_d), .e(bcd_to_7_seg_1_e), .f(bcd_to_7_seg_1_f), .g(bcd_to_7_seg_1_g));
  _7_Segment_Display u_7_segment_display_1 (
    .g(bcd_to_7_seg_1_g), .f(bcd_to_7_seg_1_f), .a(bcd_to_7_seg_1_a), .b(bcd_to_7_seg_1_b),
    .e(bcd_to_7_seg_1_e), .d(bcd_to_7_seg_1_d), .c(bcd_to_7_seg_1_c));  // open: dp

  // Notes on the sheet:
  //   DIVISION BY ZERO FLAG
endmodule

module _4_bit_Comparator (
  input  [3:0] in_1,
  input  [3:0] in_2,
  output L,
  output E
);

  wire and_1_out, and_2_out, and_3_out, and_4_out, and_5_out, and_6_out, and_7_out, and_8_out,
       n1_bit_comparator_1_e, n1_bit_comparator_1_l, n1_bit_comparator_2_e, n1_bit_comparator_2_l,
       n1_bit_comparator_3_e, n1_bit_comparator_3_l, n1_bit_comparator_4_e, n1_bit_comparator_4_l, or_1_out,
       or_2_out;

  _1_bit_Comparator u_1_bit_comparator_1 (
    .A(in_1[0]), .B(in_2[0]), .L(n1_bit_comparator_1_l), .E(n1_bit_comparator_1_e));
  _1_bit_Comparator u_1_bit_comparator_2 (
    .A(in_1[1]), .B(in_2[1]), .L(n1_bit_comparator_2_l), .E(n1_bit_comparator_2_e));
  _1_bit_Comparator u_1_bit_comparator_3 (
    .A(in_1[2]), .B(in_2[2]), .L(n1_bit_comparator_3_l), .E(n1_bit_comparator_3_e));
  _1_bit_Comparator u_1_bit_comparator_4 (
    .A(in_1[3]), .B(in_2[3]), .L(n1_bit_comparator_4_l), .E(n1_bit_comparator_4_e));
  and and_1 (and_1_out, n1_bit_comparator_1_l, n1_bit_comparator_2_e);
  and and_2 (and_2_out, n1_bit_comparator_3_e, n1_bit_comparator_4_e);
  and and_3 (and_3_out, n1_bit_comparator_3_e, n1_bit_comparator_4_e);
  and and_4 (and_4_out, n1_bit_comparator_3_l, n1_bit_comparator_4_e);
  and and_5 (and_5_out, n1_bit_comparator_4_e, n1_bit_comparator_3_e);
  and and_6 (and_6_out, n1_bit_comparator_2_e, n1_bit_comparator_1_e);
  and and_7 (and_7_out, and_1_out, and_2_out);
  and and_8 (and_8_out, n1_bit_comparator_2_l, and_3_out);
  and and_9 (E, and_5_out, and_6_out);
  or or_1 (or_1_out, and_7_out, and_8_out);
  or or_2 (or_2_out, and_4_out, n1_bit_comparator_4_l);
  or or_3 (L, or_1_out, or_2_out);

  // Notes on the sheet:
  //   0
  //   1
  //   2
  //   3
endmodule

module _1_bit_Comparator (
  input  A,
  input  B,
  output L,
  output E
);

  wire and_2_out, and_3_out, not_1_out, not_2_out;

  not not_1 (not_1_out, A);
  not not_2 (not_2_out, B);
  and and_1 (L, not_2_out, A);
  and and_2 (and_2_out, A, B);
  and and_3 (and_3_out, not_1_out, not_2_out);
  or or_1 (E, and_2_out, and_3_out);
endmodule

module Half_Adder (
  input  A,
  input  B,
  output S,
  output out_4
);

  xor xor_1 (S, A, B);
  and and_1 (out_4, A, B);

  // Notes on the sheet:
  //   C
endmodule

module Full_Adder (
  input  in_1,
  input  in_2,
  input  in_3,
  output out_4,
  output out_5
);

  wire half_adder_1_out_4, half_adder_1_s, half_adder_2_out_4;

  Half_Adder half_adder_1 (.A(in_1), .B(in_2), .S(half_adder_1_s), .out_4(half_adder_1_out_4));
  Half_Adder half_adder_2 (.A(half_adder_1_s), .B(in_3), .S(out_4), .out_4(half_adder_2_out_4));
  or or_1 (out_5, half_adder_2_out_4, half_adder_1_out_4);
endmodule

module Subtractor (
  input  [3:0] B,
  input  [3:0] A,
  output [3:0] out_3
);

  wire full_adder_1_out_5, full_adder_2_out_5, full_adder_3_out_5, full_adder_4_out_5, xor_1_out, xor_2_out,
       xor_3_out, xor_4_out;

  xor xor_1 (xor_1_out, B[3], 1'b1);
  Full_Adder full_adder_1 (
    .in_1(full_adder_2_out_5), .in_2(A[3]), .in_3(xor_1_out), .out_4(out_3[3]), .out_5(full_adder_1_out_5));
  xor xor_2 (xor_2_out, B[2], 1'b1);
  Full_Adder full_adder_2 (
    .in_1(full_adder_3_out_5), .in_2(A[2]), .in_3(xor_2_out), .out_4(out_3[2]), .out_5(full_adder_2_out_5));
  xor xor_3 (xor_3_out, 1'b1, B[1]);
  Full_Adder full_adder_3 (
    .in_1(full_adder_4_out_5), .in_2(A[1]), .in_3(xor_3_out), .out_4(out_3[1]), .out_5(full_adder_3_out_5));
  xor xor_4 (xor_4_out, 1'b1, B[0]);
  Full_Adder full_adder_4 (.in_1(1'b1), .in_2(A[0]), .in_3(xor_4_out), .out_4(out_3[0]), .out_5(full_adder_4_out_5));
endmodule

module Divider (
  input  [4:0] DIVIDEND,
  input  [4:0] DIVISOR,
  input  in_3,
  output SIGN_FLAG,
  output out_5,
  output [4:0] out_6,
  output out_7
);

  wire n4_bit_comparator_1_e, n4_bit_comparator_2_e, n4_bit_comparator_2_l, n4_bit_comparator_3_e,
       n4_bit_comparator_3_l, n4_bit_comparator_4_e, n4_bit_comparator_4_l, n4_bit_comparator_5_e,
       n4_bit_comparator_5_l, n4_bit_comparator_6_e;
  wire [3:0] and_8_out, and_11_out, and_12_out, subtractor_3_out_3;
  wire [3:1] subtractor_1_out_3, subtractor_2_out_3;
  wire [3:3] subtractor_1_out_3_2, subtractor_2_out_3_2;
  wire [4:0] or_4_out;

  and and_1 (and_8_out[3], or_4_out[3], DIVISOR[3]);
  and and_2 (and_11_out[3], or_4_out[2], DIVISOR[3]);
  and and_3 (and_12_out[3], or_4_out[1], DIVISOR[3]);
  and and_4 (and_8_out[2], or_4_out[3], DIVISOR[2]);
  and and_5 (and_8_out[1], or_4_out[3], DIVISOR[1]);
  and and_6 (and_11_out[2], or_4_out[2], DIVISOR[2]);
  and and_7 (and_12_out[2], or_4_out[1], DIVISOR[2]);
  and and_8 (and_8_out[0], or_4_out[3], DIVISOR[0]);
  and and_9 (and_11_out[1], or_4_out[2], DIVISOR[1]);
  and and_10 (and_12_out[1], or_4_out[1], DIVISOR[1]);
  _4_bit_Comparator u_4_bit_comparator_1 (.in_1(4'b0000), .in_2(DIVISOR[3:0]), .E(n4_bit_comparator_1_e));  // open: L
  Subtractor subtractor_1 (
    .B(and_8_out), .A({3'b000, DIVIDEND[3]}), .out_3({subtractor_1_out_3_2[3], subtractor_1_out_3}));
  and and_11 (and_11_out[0], or_4_out[2], DIVISOR[0]);
  and and_12 (and_12_out[0], or_4_out[1], DIVISOR[0]);
  _4_bit_Comparator u_4_bit_comparator_2 (
    .in_1({3'b000, DIVIDEND[3]}), .in_2(DIVISOR[3:0]), .L(n4_bit_comparator_2_l), .E(n4_bit_comparator_2_e));
  or or_1 (or_4_out[3], n4_bit_comparator_2_l, n4_bit_comparator_2_e);
  and and_13 (out_7, in_3, n4_bit_comparator_1_e);
  Subtractor subtractor_2 (
    .B(and_11_out), .A({subtractor_1_out_3, DIVIDEND[2]}),
    .out_3({subtractor_2_out_3_2[3], subtractor_2_out_3}));
  Subtractor subtractor_3 (.B(and_12_out), .A({subtractor_2_out_3, DIVIDEND[1]}), .out_3(subtractor_3_out_3));
  _4_bit_Comparator u_4_bit_comparator_3 (
    .in_1({subtractor_1_out_3, DIVIDEND[2]}), .in_2(DIVISOR[3:0]), .L(n4_bit_comparator_3_l),
    .E(n4_bit_comparator_3_e));
  or or_2 (or_4_out[2], n4_bit_comparator_3_l, n4_bit_comparator_3_e);
  _4_bit_Comparator u_4_bit_comparator_4 (
    .in_1({subtractor_2_out_3, DIVIDEND[1]}), .in_2(DIVISOR[3:0]), .L(n4_bit_comparator_4_l),
    .E(n4_bit_comparator_4_e));
  _4_bit_Comparator u_4_bit_comparator_5 (
    .in_1({subtractor_3_out_3[2:0], DIVIDEND[0]}), .in_2(DIVISOR[3:0]), .L(n4_bit_comparator_5_l),
    .E(n4_bit_comparator_5_e));
  or or_3 (or_4_out[1], n4_bit_comparator_4_l, n4_bit_comparator_4_e);
  or or_4 (or_4_out[0], n4_bit_comparator_5_l, n4_bit_comparator_5_e);
  xor xor_1 (or_4_out[4], DIVISOR[4], DIVIDEND[4]);
  and and_14 (SIGN_FLAG, or_4_out[4], in_3);
  and and_15 (out_6[3], in_3, or_4_out[3]);
  and and_16 (out_6[4], in_3, or_4_out[4]);
  and and_17 (out_6[2], in_3, or_4_out[2]);
  _4_bit_Comparator u_4_bit_comparator_6 (.in_1(4'b0000), .in_2(or_4_out[3:0]), .E(n4_bit_comparator_6_e));  // open: L
  and and_18 (out_6[1], in_3, or_4_out[1]);
  and and_19 (out_5, n4_bit_comparator_6_e, in_3);
  and and_20 (out_6[0], in_3, or_4_out[0]);

  // Notes on the sheet:
  //   DIVISION BY ZERO FLAG
  //   RESULT
endmodule

module BCD_to_7_SEG (
  input  [3:0] in_1,
  output a,
  output b,
  output c,
  output d,
  output e,
  output f,
  output g
);

  wire and_1_out, and_2_out, and_3_out, and_4_out, and_5_out, and_6_out, and_7_out, and_8_out, and_9_out,
       and_10_out, and_11_out, and_12_out, and_13_out, and_14_out, and_15_out, and_16_out, not_1_out,
       not_2_out, not_3_out, not_4_out, or_1_out, or_2_out, or_3_out, or_4_out, or_5_out, or_6_out, or_8_out,
       or_12_out, or_13_out;

  not not_1 (not_1_out, in_1[3]);
  not not_2 (not_2_out, in_1[2]);
  not not_3 (not_3_out, in_1[1]);
  not not_4 (not_4_out, in_1[0]);
  and and_1 (and_1_out, not_1_out, in_1[2]);
  and and_2 (and_2_out, not_2_out, not_3_out);
  and and_3 (and_3_out, in_1[1], not_1_out);
  and and_4 (and_4_out, and_1_out, in_1[0]);
  and and_5 (and_5_out, and_2_out, not_4_out);
  and and_6 (and_6_out, and_2_out, in_1[3]);
  and and_7 (and_7_out, not_1_out, not_2_out);
  and and_8 (and_8_out, not_1_out, not_3_out);
  and and_9 (and_9_out, and_8_out, not_4_out);
  and and_10 (and_10_out, and_3_out, in_1[0]);
  and and_11 (and_11_out, not_1_out, in_1[0]);
  and and_12 (and_12_out, and_3_out, not_4_out);
  and and_13 (and_13_out, and_7_out, in_1[1]);
  and and_14 (and_14_out, and_4_out, not_3_out);
  and and_15 (and_15_out, and_1_out, not_3_out);
  and and_16 (and_16_out, and_1_out, not_4_out);
  or or_1 (or_1_out, and_3_out, and_4_out);
  or or_2 (or_2_out, and_5_out, and_6_out);
  or or_3 (or_3_out, and_6_out, and_9_out);
  or or_4 (or_4_out, and_7_out, and_10_out);
  or or_5 (or_5_out, and_1_out, and_11_out);
  or or_6 (or_6_out, and_12_out, and_13_out);
  or or_7 (e, and_5_out, and_12_out);
  or or_8 (or_8_out, and_15_out, and_16_out);
  or or_9 (a, or_1_out, or_2_out);
  or or_10 (b, or_3_out, or_4_out);
  or or_11 (c, or_2_out, or_5_out);
  or or_12 (or_12_out, or_6_out, and_14_out);
  or or_13 (or_13_out, and_6_out, and_15_out);
  or or_14 (d, or_2_out, or_12_out);
  or or_15 (f, or_3_out, or_8_out);
  or or_16 (g, or_6_out, or_13_out);

  // Notes on the sheet:
  //   A
  //   B
  //   D
  //   C
endmodule
