// Logisim project Final_Adder.circ as structural Verilog: 6 circuits, main circuit half Adder
module half_Adder (
  input  A,
  input  B,
  output S,
  output out_4
);

  xor xor_1 (S, A, B);
  and and_1 (out_4, A, B);

  // Notes on the sheet:
  //   C
endmodule

module Full_Adder (
  input  in_1,
  input  in_2,
  input  in_3,
  output out_4,
  output out_5
);

  wire half_adder_1_out_4, half_adder_1_s, half_adder_2_out_4;

  half_Adder half_adder_1 (.A(in_1), .B(in_2), .S(half_adder_1_s), .out_4(half_adder_1_out_4));
  half_Adder half_adder_2 (.A(half_adder_1_s), .B(in_3), .S(out_4), .out_4(half_adder_2_out_4));
  or or_1 (out_5, half_adder_2_out_4, half_adder_1_out_4);
endmodule

module Addition (
  input  [4:0] A,
  input  [4:0] B,
  input  in_3,
  output [5:0] out_4
);

  wire full_adder_2_out_5, full_adder_3_out_5, full_adder_4_out_5, full_adder_5_out_5, half_adder_1_out_4;
  wire [5:0] a_2_s_complement_1_out_2, a_2_s_complement_2_out_2, half_adder_1_s, result_complement_1_out_2;

  Full_Adder full_adder_1 (
    .in_1(full_adder_2_out_5), .in_2(a_2_s_complement_2_out_2[5]), .in_3(a_2_s_complement_1_out_2[5]),
    .out_4(half_adder_1_s[5]));  // open: out_5
  Full_Adder full_adder_2 (
    .in_1(full_adder_3_out_5), .in_2(a_2_s_complement_2_out_2[4]), .in_3(a_2_s_complement_1_out_2[4]),
    .out_4(half_adder_1_s[4]), .out_5(full_adder_2_out_5));
  Full_Adder full_adder_3 (
    .in_1(a_2_s_complement_2_out_2[3]), .in_2(full_adder_4_out_5), .in_3(a_2_s_complement_1_out_2[3]),
    .out_4(half_adder_1_s[3]), .out_5(full_adder_3_out_5));
  and and_1 (out_4[5], result_complement_1_out_2[5], in_3);
  A_2_s_complement a_2_s_complement_1 (.in_1(A), .out_2(a_2_s_complement_1_out_2));
  Full_Adder full_adder_4 (
    .in_1(full_adder_5_out_5), .in_2(a_2_s_complement_2_out_2[2]), .in_3(a_2_s_complement_1_out_2[2]),
    .out_4(half_adder_1_s[2]), .out_5(full_adder_4_out_5));
  A_2_s_complement a_2_s_complement_2 (.in_1(B), .out_2(a_2_s_complement_2_out_2));
  Result_complement result_complement_1 (.in_1(half_adder_1_s), .out_2(result_complement_1_out_2));
  and and_2 (out_4[4], result_complement_1_out_2[4], in_3);
  and and_3 (out_4[3], result_complement_1_out_2[3], in_3);
  Full_Adder full_adder_5 (
    .in_1(half_adder_1_out_4), .in_2(a_2_s_complement_1_out_2[1]), .in_3(a_2_s_complement_2_out_2[1]),
    .out_4(half_adder_1_s[1]), .out_5(full_adder_5_out_5));
  and and_4 (out_4[2], result_complement_1_out_2[2], in_3);
  half_Adder half_adder_1 (
    .A(a_2_s_complement_1_out_2[0]), .B(a_2_s_complement_2_out_2[0]), .S(half_adder_1_s[0]),
    .out_4(half_adder_1_out_4));
  and and_5 (out_4[1], result_complement_1_out_2[1], in_3);
  and and_6 (out_4[0], result_complement_1_out_2[0], in_3);
endmodule

module B_2_s_complement (
  input  [4:0] in_1,
  output [4:0] out_2
);

  wire half_adder_2_out_4, half_adder_3_out_4, half_adder_4_out_4, xor_1_out, xor_2_out, xor_3_out,
       xor_4_out, xor_5_out;

  xor xor_1 (xor_1_out, in_1[4], 1'b0);
  xor xor_2 (xor_2_out, xor_1_out, in_1[3]);
  half_Adder half_adder_1 (.A(half_adder_2_out_4), .B(xor_2_out), .S(out_2[3]));  // open: out_4
  xor xor_3 (xor_3_out, xor_1_out, in_1[2]);
  half_Adder half_adder_2 (.A(half_adder_3_out_4), .B(xor_3_out), .S(out_2[2]), .out_4(half_adder_2_out_4));
  xor xor_4 (xor_4_out, xor_1_out, in_1[1]);
  half_Adder half_adder_3 (.A(half_adder_4_out_4), .B(xor_4_out), .S(out_2[1]), .out_4(half_adder_3_out_4));
  xor xor_5 (xor_5_out, xor_1_out, in_1[0]);
  half_Adder half_adder_4 (.A(xor_1_out), .B(xor_5_out), .S(out_2[0]), .out_4(half_adder_4_out_4));

  assign out_2[4] = in_1[4];
endmodule

module A_2_s_complement (
  input  [4:0] in_1,
  output [5:0] out_2
);

  wire half_adder_2_out_4, half_adder_3_out_4, half_adder_4_out_4, half_adder_5_out_4, xor_1_out, xor_2_out,
       xor_3_out, xor_4_out, xor_5_out;

  xor xor_1 (xor_1_out, in_1[4], 1'b0);
  half_Adder half_adder_1 (.A(half_adder_2_out_4), .B(xor_1_out), .S(out_2[4]));  // open: out_4
  xor xor_2 (xor_2_out, in_1[4], in_1[3]);
  half_Adder half_adder_2 (.A(half_adder_3_out_4), .B(xor_2_out), .S(out_2[3]), .out_4(half_adder_2_out_4));
  xor xor_3 (xor_3_out, in_1[4], in_1[2]);
  half_Adder half_adder_3 (.A(half_adder_4_out_4), .B(xor_3_out), .S(out_2[2]), .out_4(half_adder_3_out_4));
  xor xor_4 (xor_4_out, in_1[4], in_1[1]);
  half_Adder half_adder_4 (.A(half_adder_5_out_4), .B(xor_4_out), .S(out_2[1]), .out_4(half_adder_4_out_4));
  xor xor_5 (xor_5_out, in_1[4], in_1[0]);
  half_Adder half_adder_5 (.A(in_1[4]), .B(xor_5_out), .S(out_2[0]), .out_4(half_adder_5_out_4));

  assign out_2[5] = in_1[4];
endmodule

module Result_complement (
  input  [5:0] in_1,
  output [5:0] out_2
);

  wire half_adder_2_out_4, half_adder_3_out_4, half_adder_4_out_4, half_adder_5_out_4, xor_1_out, xor_2_out,
       xor_3_out, xor_4_out, xor_5_out;

  xor xor_1 (xor_1_out, in_1[5], in_1[4]);
  half_Adder half_adder_1 (.A(half_adder_2_out_4), .B(xor_1_out), .S(out_2[4]));  // open: out_4
  xor xor_2 (xor_2_out, in_1[5], in_1[3]);
  half_Adder half_adder_2 (.A(half_adder_3_out_4), .B(xor_2_out), .S(out_2[3]), .out_4(half_adder_2_out_4));
  xor xor_3 (xor_3_out, in_1[5], in_1[2]);
  half_Adder half_adder_3 (.A(half_adder_4_out_4), .B(xor_3_out), .S(out_2[2]), .out_4(half_adder_3_out_4));
  xor xor_4 (xor_4_out, in_1[5], in_1[1]);
  half_Adder half_adder_4 (.A(half_adder_5_out_4), .B(xor_4_out), .S(out_2[1]), .out_4(half_adder_4_out_4));
  xor xor_5 (xor_5_out, in_1[5], in_1[0]);
  half_Adder half_adder_5 (.A(in_1[5]), .B(xor_5_out), .S(out_2[0]), .out_4(half_adder_5_out_4));

  assign out_2[5] = in_1[5];
endmodule
