// Logisim project Multiplier & Binary to BCD.circ as structural Verilog: 6 circuits, main circuit Full Adder
module main (
  input  [4:0] in_1,
  input  [4:0] in_2,
  output sign,
  output [3:0] out_4,
  output [3:0] out_5,
  output [3:0] out_6
);

  wire [7:0] binary_to_bcd_1_p2;

  // _4by4_Bit_Multiplier 4by4_bit_multiplier_1: pin names not known; wires that end beside it: sign, binary_to_bcd_1_p2[7], binary_to_bcd_1_p2[6], in_2, binary_to_bcd_1_p2[5], in_1, binary_to_bcd_1_p2[4], binary_to_bcd_1_p2[3], binary_to_bcd_1_p2[2], binary_to_bcd_1_p2[1]
  // Binary_to_BCD binary_to_bcd_1: pin names not known; wires that end beside it: out_4, binary_to_bcd_1_p2, out_6, out_6, out_5
endmodule

module Full_Adder (
  input  in_1,
  input  in_2,
  input  in_3,
  output SUM,
  output Carry
);

  wire and_1_out, and_2_out, xor_1_out;

  xor xor_1 (xor_1_out, in_1, in_2);
  and and_1 (and_1_out, in_1, in_2);
  xor xor_2 (SUM, xor_1_out, in_3);
  and and_2 (and_2_out, xor_1_out, in_3);
  or or_1 (Carry, and_2_out, and_1_out);
endmodule

module _4_Bit_Adder (
  input  B3,
  input  A3,
  input  B2,
  input  A2,
  input  B1,
  input  A1,
  input  B0,
  input  A0,
  output out_9,
  output out_10,
  output out_11,
  output out_12,
  output out_13
);

  wire full_adder_2_carry, full_adder_3_carry, full_adder_4_carry;

  Full_Adder full_adder_1 (.in_1(full_adder_2_carry), .in_2(A3), .in_3(B3), .SUM(out_10), .Carry(out_9));
  Full_Adder full_adder_2 (.in_1(full_adder_3_carry), .in_2(A2), .in_3(B2), .SUM(out_11), .Carry(full_adder_2_carry));
  Full_Adder full_adder_3 (.in_1(full_adder_4_carry), .in_2(A1), .in_3(B1), .SUM(out_12), .Carry(full_adder_3_carry));
  Full_Adder full_adder_4 (.in_1(1'b0), .in_2(A0), .in_3(B0), .SUM(out_13), .Carry(full_adder_4_carry));
endmodule

module _4by4_Bit_Multiplier (
  input  [4:0] in_1,
  input  [4:0] in_2,
  input  in_3,
  output [8:0] out_4
);

  wire and_1_out, and_2_out, and_4_out, and_5_out, and_7_out, and_9_out, and_10_out, and_12_out, and_13_out,
       and_15_out, and_16_out, and_18_out, and_19_out, and_21_out, and_22_out, and_24_out,
       n4_bit_adder_1_out_9, n4_bit_adder_1_out_10, n4_bit_adder_1_out_11, n4_bit_adder_1_out_12,
       n4_bit_adder_1_out_13, n4_bit_adder_2_out_9, n4_bit_adder_2_out_10, n4_bit_adder_2_out_11,
       n4_bit_adder_2_out_12, n4_bit_adder_2_out_13, n4_bit_adder_3_out_9, n4_bit_adder_3_out_10,
       n4_bit_adder_3_out_11, n4_bit_adder_3_out_12, n4_bit_adder_3_out_13, xor_1_out;

  and and_1 (and_1_out, in_2[3], in_1[3]);
  and and_2 (and_2_out, in_1[2], in_2[3]);
  xor xor_1 (xor_1_out, in_2[4], in_1[4]);
  and and_3 (out_4[8], xor_1_out, in_3);
  and and_4 (and_4_out, in_1[0], in_2[3]);
  and and_5 (and_5_out, in_1[1], in_2[3]);
  and and_6 (out_4[7], n4_bit_adder_1_out_9, in_3);
  and and_7 (and_7_out, in_1[3], in_2[2]);
  _4_Bit_Adder u_4_bit_adder_1 (
    .B3(and_1_out), .A3(n4_bit_adder_2_out_9), .B2(and_2_out), .A2(n4_bit_adder_2_out_10), .B1(and_5_out),
    .A1(n4_bit_adder_2_out_11), .B0(and_4_out), .A0(n4_bit_adder_2_out_12), .out_9(n4_bit_adder_1_out_9),
    .out_10(n4_bit_adder_1_out_10), .out_11(n4_bit_adder_1_out_11), .out_12(n4_bit_adder_1_out_12),
    .out_13(n4_bit_adder_1_out_13));
  and and_8 (out_4[6], n4_bit_adder_1_out_10, in_3);
  and and_9 (and_9_out, in_1[1], in_2[2]);
  and and_10 (and_10_out, in_1[2], in_2[2]);
  and and_11 (out_4[5], n4_bit_adder_1_out_11, in_3);
  and and_12 (and_12_out, in_2[1], in_1[3]);
  and and_13 (and_13_out, in_1[0], in_2[2]);
  and and_14 (out_4[4], n4_bit_adder_1_out_12, in_3);
  and and_15 (and_15_out, in_2[1], in_1[2]);
  _4_Bit_Adder u_4_bit_adder_2 (
    .B3(and_7_out), .A3(n4_bit_adder_3_out_9), .B2(and_10_out), .A2(n4_bit_adder_3_out_10), .B1(and_9_out),
    .A1(n4_bit_adder_3_out_11), .B0(and_13_out), .A0(n4_bit_adder_3_out_12), .out_9(n4_bit_adder_2_out_9),
    .out_10(n4_bit_adder_2_out_10), .out_11(n4_bit_adder_2_out_11), .out_12(n4_bit_adder_2_out_12),
    .out_13(n4_bit_adder_2_out_13));
  and and_16 (and_16_out, in_2[1], in_1[1]);
  and and_17 (out_4[3], n4_bit_adder_1_out_13, in_3);
  and and_18 (and_18_out, in_2[1], in_1[0]);
  _4_Bit_Adder u_4_bit_adder_3 (
    .B3(and_12_out), .A3(1'b0), .B2(and_15_out), .A2(and_19_out), .B1(and_16_out), .A1(and_22_out),
    .B0(and_18_out), .A0(and_21_out), .out_9(n4_bit_adder_3_out_9), .out_10(n4_bit_adder_3_out_10),
    .out_11(n4_bit_adder_3_out_11), .out_12(n4_bit_adder_3_out_12), .out_13(n4_bit_adder_3_out_13));
  and and_19 (and_19_out, in_2[0], in_1[3]);
  and and_20 (out_4[2], n4_bit_adder_2_out_13, in_3);
  and and_21 (and_21_out, in_2[0], in_1[1]);
  and and_22 (and_22_out, in_2[0], in_1[2]);
  and and_23 (out_4[1], n4_bit_adder_3_out_13, in_3);
  and and_24 (and_24_out, in_2[0], in_1[0]);
  and and_25 (out_4[0], and_24_out, in_3);
endmodule

module Binary_to_BCD (
  input  [7:0] in_1,
  output [3:0] out_2,
  output [3:0] out_3,
  output [3:0] out_4
);

  wire n3_adder_shifter_1_s0, n3_adder_shifter_1_s1, n3_adder_shifter_1_s2, n3_adder_shifter_1_s3,
       n3_adder_shifter_2_s0, n3_adder_shifter_2_s1, n3_adder_shifter_2_s2, n3_adder_shifter_2_s3,
       n3_adder_shifter_3_s0, n3_adder_shifter_3_s1, n3_adder_shifter_3_s2, n3_adder_shifter_4_s0,
       n3_adder_shifter_4_s1, n3_adder_shifter_4_s2, n3_adder_shifter_4_s3, n3_adder_shifter_5_s0,
       n3_adder_shifter_5_s1, n3_adder_shifter_5_s2, n3_adder_shifter_5_s3;

  _3_Adder___shifter u_3_adder_shifter_1 (
    .A0(in_1[5]), .A1(in_1[6]), .A2(in_1[7]), .A3(1'b0), .S0(n3_adder_shifter_1_s0),
    .S1(n3_adder_shifter_1_s1), .S2(n3_adder_shifter_1_s2), .S3(n3_adder_shifter_1_s3));
  _3_Adder___shifter u_3_adder_shifter_2 (
    .A0(in_1[4]), .A1(n3_adder_shifter_1_s0), .A2(n3_adder_shifter_1_s1), .A3(n3_adder_shifter_1_s2),
    .S0(n3_adder_shifter_2_s0), .S1(n3_adder_shifter_2_s1), .S2(n3_adder_shifter_2_s2),
    .S3(n3_adder_shifter_2_s3));
  _3_Adder___shifter u_3_adder_shifter_3 (
    .A0(n3_adder_shifter_4_s3), .A1(n3_adder_shifter_2_s3), .A2(n3_adder_shifter_1_s3), .A3(1'b0),
    .S0(n3_adder_shifter_3_s0), .S1(n3_adder_shifter_3_s1), .S2(n3_adder_shifter_3_s2), .S3(out_2[1]));
  _3_Adder___shifter u_3_adder_shifter_4 (
    .A0(in_1[3]), .A1(n3_adder_shifter_2_s0), .A2(n3_adder_shifter_2_s1), .A3(n3_adder_shifter_2_s2),
    .S0(n3_adder_shifter_4_s0), .S1(n3_adder_shifter_4_s1), .S2(n3_adder_shifter_4_s2),
    .S3(n3_adder_shifter_4_s3));
  _3_Adder___shifter u_3_adder_shifter_5 (
    .A0(in_1[2]), .A1(n3_adder_shifter_4_s0), .A2(n3_adder_shifter_4_s1), .A3(n3_adder_shifter_4_s2),
    .S0(n3_adder_shifter_5_s0), .S1(n3_adder_shifter_5_s1), .S2(n3_adder_shifter_5_s2),
    .S3(n3_adder_shifter_5_s3));
  _3_Adder___shifter u_3_adder_shifter_6 (
    .A0(n3_adder_shifter_5_s3), .A1(n3_adder_shifter_3_s0), .A2(n3_adder_shifter_3_s1),
    .A3(n3_adder_shifter_3_s2), .S0(out_3[1]), .S1(out_3[2]), .S2(out_3[3]), .S3(out_2[0]));
  _3_Adder___shifter u_3_adder_shifter_7 (
    .A0(in_1[1]), .A1(n3_adder_shifter_5_s0), .A2(n3_adder_shifter_5_s1), .A3(n3_adder_shifter_5_s2),
    .S0(out_4[1]), .S1(out_4[2]), .S2(out_4[3]), .S3(out_3[0]));

  assign out_2[3:2] = 2'b00;
  assign out_4[0] = in_1[0];
endmodule

module _3_Adder___shifter (
  input  A0,
  input  A1,
  input  A2,
  input  A3,
  output S0,
  output S1,
  output S2,
  output S3
);

  wire and_1_out, and_2_out, and_3_out, and_4_out, and_5_out, and_6_out, and_7_out, and_8_out, and_9_out,
       and_10_out, not_1_out, not_2_out, not_3_out, not_4_out;

  not not_1 (not_1_out, A0);
  not not_2 (not_2_out, A1);
  not not_3 (not_3_out, A2);
  not not_4 (not_4_out, A3);
  and and_1 (and_1_out, not_1_out, A3);
  and and_2 (and_2_out, not_1_out, A1, A2);
  and and_3 (and_3_out, A0, not_3_out, not_4_out);
  or or_1 (S0, and_1_out, and_2_out, and_3_out);
  and and_4 (and_4_out, A1, not_3_out);
  and and_5 (and_5_out, A0, A1);
  and and_6 (and_6_out, not_1_out, A3);
  and and_7 (and_7_out, A3, A0);
  and and_8 (and_8_out, not_1_out, not_2_out, A2);
  and and_9 (and_9_out, A0, A2);
  and and_10 (and_10_out, A1, A2);
  or or_2 (S1, and_4_out, and_5_out, and_6_out);
  or or_3 (S2, and_7_out, and_8_out);
  or or_4 (S3, and_9_out, and_10_out, A3);
  // OR_Gate or_5 is placed but not wired
endmodule
